// Logisim project hw4.circ as structural Verilog: 11 circuits, main circuit main
module main (
  input  reset
);

  wire and_1_out, and_2_out, beq_enb, bgt_enb, clk, Isel, J_enb, Jal_enb, Jr_enb, Kb_enb, keyboard_1_avail,
       lw_enb, mem_WE, memorylatch_1_oe_latched, memorylatch_1_we_latched, not_1_out, not_2_out, not_3_out,
       or_1_out, posOut, reg_WE, TTY_enb, zeroOut;
  wire [2:0] multiplexer_6_out, multiplexer_7_out, opType, rd, rs, rt, shift;
  wire [5:0] Imm;
  wire [6:0] keyboard_1_data;
  wire [7:0] kbd_ext;
  wire [11:0] add;
  wire [15:0] ader_2_result, ALU_out, Command, curPC, mem_out, memorylatch_1_address_latched,
       memorylatch_1_data_in_latched, multiplexer_1_out, multiplexer_2_out, multiplexer_5_out,
       multiplexer_8_out, multiplexer_9_out, multiplexer_10_out, next_pc, pc_plus1, registerfile_1_rs1_data,
       rt_dat, SignExt;

  Clock clock_1 (.out(clk));
  Multiplexer #(.width(16), .enable("false")) multiplexer_1 (
    .in0(next_pc), .in1(ALU_out), .out(multiplexer_1_out), .sel(Jr_enb));
  ader ader_1 (.sub(1'b0), .A(curPC), .B(16'h1), .result(pc_plus1));  // open: ovf
  Reg reg_1 (.data_in(multiplexer_1_out), .clk(clk), .reset(reset), .data_out(curPC), .WE(1'b1));
  signX signx_1 (.Imm(Imm), .signX(SignExt));
  TTY #(.rows(13), .cols(80), .trigger("falling")) tty_1 (.data(ALU_out[6:0]), .clk(clk), .we(TTY_enb), .clr(reset));
  ROM #(.addrWidth(16), .dataWidth(16)) rom_1 (.addr(curPC), .data(Command));
  ader ader_2 (.sub(1'b0), .A(SignExt), .B(pc_plus1), .result(ader_2_result));  // open: ovf
  Keyboard keyboard_1 (.clk(clk), .re(Kb_enb), .clr(reset), .avail(keyboard_1_avail), .data(keyboard_1_data));
  Multiplexer #(.width(16), .enable("false")) multiplexer_2 (
    .in0(pc_plus1), .in1(ader_2_result), .out(multiplexer_2_out), .sel(or_1_out));
  or or_1 (or_1_out, and_1_out, and_2_out);
  and and_1 (and_1_out, beq_enb, zeroOut);
  and and_2 (and_2_out, bgt_enb, not_1_out, posOut);
  not not_1 (not_1_out, zeroOut);
  Multiplexer #(.width(8), .enable("false")) multiplexer_3 (
    .in0({1'b0, keyboard_1_data}), .in1(8'h80), .out(kbd_ext), .sel(not_2_out));
  not not_2 (not_2_out, keyboard_1_avail);
  Multiplexer #(.width(16), .enable("false")) multiplexer_4 (
    .in0(multiplexer_2_out), .in1({curPC[15:12], add}), .out(next_pc), .sel(J_enb));
  memoryLatch memorylatch_1 (
    .adress(ALU_out), .WE(mem_WE), .clk(clk), .dataIn(rt_dat),
    .address_latched(memorylatch_1_address_latched), .WE_latched(memorylatch_1_we_latched),
    .OE_latched(memorylatch_1_oe_latched), .data_in_latched(memorylatch_1_data_in_latched));
  Multiplexer #(.width(16), .enable("false")) multiplexer_5 (
    .in0(multiplexer_10_out), .in1({{8{1'b0}}, kbd_ext}), .out(multiplexer_5_out), .sel(Kb_enb));
  Multiplexer #(.width(3), .enable("false")) multiplexer_6 (.in0(rd), .in1(rt), .out(multiplexer_6_out), .sel(Isel));
  RAM #(.addrWidth(16), .dataWidth(16), .trigger("high"), .databus("bibus")) ram_1 (
    .addr(memorylatch_1_address_latched), .we(memorylatch_1_we_latched), .oe(memorylatch_1_oe_latched),
    .din(memorylatch_1_data_in_latched), .dout(mem_out));
  Multiplexer #(.width(3), .enable("false")) multiplexer_7 (
    .in0(multiplexer_6_out), .in1(3'b111), .out(multiplexer_7_out), .sel(Jal_enb));
  not not_3 (not_3_out, clk);
  contrl contrl_1 (
    .Input(Command), .WE(1'b1), .RegWE(reg_WE), .opType(opType), .sft(shift), .Rs(rs), .Rt(rt), .Imm(Imm),
    .addr(add), .beq_enb(beq_enb), .bgt_enb(bgt_enb), .mem_WE(mem_WE), .TTY_enb(TTY_enb), .KB_enb(Kb_enb),
    .I_enb(Isel), .J_enb(J_enb), .jr_enb(Jr_enb), .jal_enb(Jal_enb), .lw_enb(lw_enb), .rd(rd));
  RegisterFile registerfile_1 (
    .RegWriteEnable(reg_WE), .rd(multiplexer_7_out), .rs1(rs), .WriteData(multiplexer_5_out), .reset(reset),
    .rs2(rt), .clk(not_3_out), .rs1_data(registerfile_1_rs1_data), .rs2_data(rt_dat));
  Multiplexer #(.width(16), .enable("false")) multiplexer_8 (
    .in0(registerfile_1_rs1_data), .in1(pc_plus1), .out(multiplexer_8_out), .sel(Jal_enb));
  Multiplexer #(.width(16), .enable("false")) multiplexer_9 (
    .in0(rt_dat), .in1(SignExt), .out(multiplexer_9_out), .sel(Isel));
  alu alu_1 (
    .DataIn1(multiplexer_8_out), .DataIn2(multiplexer_9_out), .Shift(shift), .DataOut(ALU_out),
    .opType(opType), .beq(zeroOut), .bgt(posOut));
  Multiplexer #(.width(16), .enable("false")) multiplexer_10 (
    .in0(ALU_out), .in1(mem_out), .out(multiplexer_10_out), .sel(lw_enb));

  // Other names for the same wires on the sheet: TTY_dat[6:0] = ALU_out[6:0]; Jpc[15:0] = {curPC[15:12], add};
  //   kbd_out[7:0] = kbd_ext; res = reset
endmodule

module RegisterFile (
  input  RegWriteEnable,
  input  [2:0] rd,
  input  [2:0] rs1,
  input  [15:0] WriteData,
  input  reset,
  input  [2:0] rs2,
  input  clk,
  output [15:0] rs1_data,
  output [15:0] rs2_data
);

  wire decoder_1_out0, reg1, reg2, reg3, reg4, reg5, reg6, reg7;
  wire [15:0] out_reg1, out_reg2, out_reg3, out_reg4, out_reg5, out_reg6, out_reg7;

  Decoder #(.select(3)) decoder_1 (
    .out0(decoder_1_out0), .out1(reg1), .out2(reg2), .out3(reg3), .out4(reg4), .out5(reg5), .out6(reg6),
    .out7(reg7), .sel(rd), .en(RegWriteEnable));
  // Probe on {16{1'b0}}
  // Probe on out_reg1
  Reg reg_1 (.data_in(WriteData), .clk(clk), .reset(reset), .data_out(out_reg1), .WE(reg1));
  // Probe on out_reg2
  Reg reg_2 (.data_in(WriteData), .clk(clk), .reset(reset), .data_out(out_reg2), .WE(reg2));
  // Probe on out_reg3
  Reg reg_3 (.data_in(WriteData), .clk(clk), .reset(reset), .data_out(out_reg3), .WE(reg3));
  // Probe on out_reg4
  Reg reg_4 (.data_in(WriteData), .clk(clk), .reset(reset), .data_out(out_reg4), .WE(reg4));
  // Probe on out_reg5
  Reg reg_5 (.data_in(WriteData), .clk(clk), .reset(reset), .data_out(out_reg5), .WE(reg5));
  Reg reg_6 (.data_in(WriteData), .clk(clk), .reset(reset), .data_out(out_reg6), .WE(reg6));
  // Probe on out_reg7
  Reg reg_7 (.data_in(WriteData), .clk(clk), .reset(reset), .data_out(out_reg7), .WE(reg7));
  // Probe on out_reg6
  Multiplexer #(.select(3), .width(16), .enable("false")) multiplexer_1 (
    .in0({16{1'b0}}), .in1(out_reg1), .in2(out_reg2), .in3(out_reg3), .in4(out_reg4), .in5(out_reg5),
    .in6(out_reg6), .in7(out_reg7), .out(rs1_data), .sel(rs1));
  Multiplexer #(.select(3), .width(16), .enable("false")) multiplexer_2 (
    .in0({16{1'b0}}), .in1(out_reg1), .in2(out_reg2), .in3(out_reg3), .in4(out_reg4), .in5(out_reg5),
    .in6(out_reg6), .in7(out_reg7), .out(rs2_data), .sel(rs2));

  // Other names for the same wires on the sheet: InputData[15:0] = WriteData; res = reset
endmodule

module alu (
  input  [15:0] DataIn1,
  input  [15:0] DataIn2,
  input  [2:0] Shift,
  input  [2:0] opType,
  output [15:0] DataOut,
  output beq,
  output bgt
);

  wire [15:0] Add, \and , LeftShift, \or , RightShift, Subtract;

  assign \or  = DataIn1 | DataIn2;  // OR_Gate or_1, 16 bits wide
  assign \and  = DataIn1 & DataIn2;  // AND_Gate and_1, 16 bits wide
  ader ader_1 (.sub(1'b0), .A(DataIn1), .B(DataIn2), .result(Add));  // open: ovf
  ader ader_2 (.sub(1'b1), .A(DataIn1), .B(DataIn2), .result(Subtract));  // open: ovf
  R_BarrelShifter r_barrelshifter_1 (.data_in(DataIn1), .bitstoShift(Shift), .shifted_data(RightShift));
  L_Shifter l_shifter_1 (.data_in(DataIn1), .bitstoShift(Shift), .shifted_data(LeftShift));
  Multiplexer #(.select(3), .width(16), .enable("false")) multiplexer_1 (
    .in0(Add), .in1(Subtract), .in2(RightShift), .in3(LeftShift), .in4(\or ), .in5(\and ), .in6(DataIn1),
    .out(DataOut), .sel(opType));  // open: in7
  not not_1 (bgt, DataOut[15]);
  nor nor_1 (beq, DataOut[0], DataOut[1], DataOut[2], DataOut[3], DataOut[4], DataOut[5], DataOut[6], DataOut[7], DataOut[8], DataOut[9], DataOut[10], DataOut[11], DataOut[12], DataOut[13], DataOut[14], DataOut[15]);

  // Other names for the same wires on the sheet: In1[15:0] = DataIn1; In2[15:0] = DataIn2
endmodule

module Reg (
  input  [15:0] data_in,
  input  clk,
  input  WE,
  input  reset,
  output [15:0] data_out
);

  wire clkEnable;

  and and_1 (clkEnable, clk, WE);
  D_Flip_Flop d_ff_1 (.D(data_in[0]), .clk(clkEnable), .Q(data_out[0]), .reset(reset));  // open: Qn, preset
  D_Flip_Flop d_ff_2 (.D(data_in[1]), .clk(clkEnable), .Q(data_out[1]), .reset(reset));  // open: Qn, preset
  D_Flip_Flop d_ff_3 (.D(data_in[2]), .clk(clkEnable), .Q(data_out[2]), .reset(reset));  // open: Qn, preset
  D_Flip_Flop d_ff_4 (.D(data_in[3]), .clk(clkEnable), .Q(data_out[3]), .reset(reset));  // open: Qn, preset
  D_Flip_Flop d_ff_5 (.D(data_in[4]), .clk(clkEnable), .Q(data_out[4]), .reset(reset));  // open: Qn, preset
  D_Flip_Flop d_ff_6 (.D(data_in[5]), .clk(clkEnable), .Q(data_out[5]), .reset(reset));  // open: Qn, preset
  D_Flip_Flop d_ff_7 (.D(data_in[6]), .clk(clkEnable), .Q(data_out[6]), .reset(reset));  // open: Qn, preset
  D_Flip_Flop d_ff_8 (.D(data_in[7]), .clk(clkEnable), .Q(data_out[7]), .reset(reset));  // open: Qn, preset
  D_Flip_Flop d_ff_9 (.D(data_in[8]), .clk(clkEnable), .Q(data_out[8]), .reset(reset));  // open: Qn, preset
  D_Flip_Flop d_ff_10 (.D(data_in[9]), .clk(clkEnable), .Q(data_out[9]), .reset(reset));  // open: Qn, preset
  D_Flip_Flop d_ff_11 (.D(data_in[10]), .clk(clkEnable), .Q(data_out[10]), .reset(reset));  // open: Qn, preset
  D_Flip_Flop d_ff_12 (.D(data_in[11]), .clk(clkEnable), .Q(data_out[11]), .reset(reset));  // open: Qn, preset
  D_Flip_Flop d_ff_13 (.D(data_in[12]), .clk(clkEnable), .Q(data_out[12]), .reset(reset));  // open: Qn, preset
  D_Flip_Flop d_ff_14 (.D(data_in[13]), .clk(clkEnable), .Q(data_out[13]), .reset(reset));  // open: Qn, preset
  D_Flip_Flop d_ff_15 (.D(data_in[14]), .clk(clkEnable), .Q(data_out[14]), .reset(reset));  // open: Qn, preset
  D_Flip_Flop d_ff_16 (.D(data_in[15]), .clk(clkEnable), .Q(data_out[15]), .reset(reset));  // open: Qn, preset

  // Other names for the same wires on the sheet: in0 = data_in[0]; in1 = data_in[1]; in2 = data_in[2];
  //   in3 = data_in[3]; in4 = data_in[4]; in5 = data_in[5]; in6 = data_in[6]; in7 = data_in[7]; in8 = data_in[8];
  //   in9 = data_in[9]; in10 = data_in[10]; in11 = data_in[11]; in12 = data_in[12]; in13 = data_in[13];
  //   in14 = data_in[14]; in15 = data_in[15]; ot0 = data_out[0]; ot1 = data_out[1]; ot2 = data_out[2];
  //   ot3 = data_out[3]; ot4 = data_out[4]; ot5 = data_out[5]; ot6 = data_out[6]; ot7 = data_out[7];
  //   ot8 = data_out[8]; ot9 = data_out[9]; ot10 = data_out[10]; ot11 = data_out[11]; ot12 = data_out[12];
  //   ot13 = data_out[13]; ot14 = data_out[14]; ot15 = data_out[15]; res = reset
endmodule

module ader (
  input  sub,
  input  [15:0] A,
  input  [15:0] B,
  output [15:0] result,
  output ovf
);

  wire B0, B1, B2, B3, B4, B5, B6, B7, B8, B9, B10, B11, B12, B13, B14, B15, single_adder_1_outc,
       single_adder_2_outc, single_adder_3_outc, single_adder_4_outc, single_adder_5_outc,
       single_adder_6_outc, single_adder_7_outc, single_adder_8_outc, single_adder_9_outc,
       single_adder_10_outc, single_adder_11_outc, single_adder_12_outc, single_adder_13_outc,
       single_adder_14_outc, single_adder_15_outc, single_adder_16_outc;

  xor xor_1 (B10, B[10], sub);
  xor xor_2 (B11, B[11], sub);
  xor xor_3 (B12, B[12], sub);
  xor xor_4 (B13, B[13], sub);
  xor xor_5 (B14, B[14], sub);
  xor xor_6 (B15, B[15], sub);
  xor xor_7 (B2, B[2], sub);
  xor xor_8 (B3, B[3], sub);
  xor xor_9 (B4, B[4], sub);
  xor xor_10 (B5, B[5], sub);
  xor xor_11 (B6, B[6], sub);
  xor xor_12 (B7, B[7], sub);
  xor xor_13 (B8, B[8], sub);
  xor xor_14 (B9, B[9], sub);
  xor xor_15 (B0, B[0], sub);
  xor xor_16 (B1, B[1], sub);
  single_adder single_adder_1 (.inA(A[0]), .inB(B0), .inC(sub), .outSum(result[0]), .outC(single_adder_1_outc));
  single_adder single_adder_2 (
    .inA(A[8]), .inB(B8), .inC(single_adder_15_outc), .outSum(result[8]), .outC(single_adder_2_outc));
  single_adder single_adder_3 (
    .inA(A[1]), .inB(B1), .inC(single_adder_1_outc), .outSum(result[1]), .outC(single_adder_3_outc));
  single_adder single_adder_4 (
    .inA(A[9]), .inB(B9), .inC(single_adder_2_outc), .outSum(result[9]), .outC(single_adder_4_outc));
  single_adder single_adder_5 (
    .inA(A[2]), .inB(B2), .inC(single_adder_3_outc), .outSum(result[2]), .outC(single_adder_5_outc));
  single_adder single_adder_6 (
    .inA(A[10]), .inB(B10), .inC(single_adder_4_outc), .outSum(result[10]), .outC(single_adder_6_outc));
  single_adder single_adder_7 (
    .inA(A[3]), .inB(B3), .inC(single_adder_5_outc), .outSum(result[3]), .outC(single_adder_7_outc));
  single_adder single_adder_8 (
    .inA(A[11]), .inB(B11), .inC(single_adder_6_outc), .outSum(result[11]), .outC(single_adder_8_outc));
  single_adder single_adder_9 (
    .inA(A[4]), .inB(B4), .inC(single_adder_7_outc), .outSum(result[4]), .outC(single_adder_9_outc));
  single_adder single_adder_10 (
    .inA(A[12]), .inB(B12), .inC(single_adder_8_outc), .outSum(result[12]), .outC(single_adder_10_outc));
  single_adder single_adder_11 (
    .inA(A[5]), .inB(B5), .inC(single_adder_9_outc), .outSum(result[5]), .outC(single_adder_11_outc));
  single_adder single_adder_12 (
    .inA(A[13]), .inB(B13), .inC(single_adder_10_outc), .outSum(result[13]), .outC(single_adder_12_outc));
  single_adder single_adder_13 (
    .inA(A[6]), .inB(B6), .inC(single_adder_11_outc), .outSum(result[6]), .outC(single_adder_13_outc));
  single_adder single_adder_14 (
    .inA(A[14]), .inB(B14), .inC(single_adder_12_outc), .outSum(result[14]), .outC(single_adder_14_outc));
  single_adder single_adder_15 (
    .inA(A[7]), .inB(B7), .inC(single_adder_13_outc), .outSum(result[7]), .outC(single_adder_15_outc));
  single_adder single_adder_16 (
    .inA(A[15]), .inB(B15), .inC(single_adder_14_outc), .outSum(result[15]), .outC(single_adder_16_outc));
  xor xor_17 (ovf, single_adder_14_outc, single_adder_16_outc);

  // Other names for the same wires on the sheet: s0 = result[0]; s1 = result[1]; s2 = result[2]; s3 = result[3];
  //   s4 = result[4]; s5 = result[5]; s6 = result[6]; s7 = result[7]; s8 = result[8]; s9 = result[9];
  //   s10 = result[10]; s11 = result[11]; s12 = result[12]; s13 = result[13]; s14 = result[14]; s15 = result[15]
endmodule

module single_adder (
  input  inA,
  input  inB,
  input  inC,
  output outSum,
  output outC
);

  wire and_1_out, and_2_out, xor_1_out;

  and and_1 (and_1_out, inA, inB);
  xor xor_1 (xor_1_out, inA, inB);
  and and_2 (and_2_out, xor_1_out, inC);
  xor xor_2 (outSum, xor_1_out, inC);
  or or_1 (outC, and_2_out, and_1_out);
endmodule

module R_BarrelShifter (
  input  [15:0] data_in,
  input  [2:0] bitstoShift,
  output [15:0] shifted_data
);

  wire [15:0] r_shift2, r_shift4, r_shift8;

  Multiplexer #(.width(16), .enable("false")) multiplexer_1 (
    .in0(data_in), .in1({{2{data_in[15]}}, data_in[14:1]}), .out(r_shift2), .sel(bitstoShift[0]));
  Multiplexer #(.width(16), .enable("false")) multiplexer_2 (
    .in0(r_shift2), .in1({{3{r_shift2[15]}}, r_shift2[14:2]}), .out(r_shift4), .sel(bitstoShift[1]));
  Multiplexer #(.width(16), .enable("false")) multiplexer_3 (
    .in0(r_shift4), .in1({{5{r_shift4[15]}}, r_shift4[14:4]}), .out(shifted_data), .sel(bitstoShift[2]));
  Multiplexer #(.width(16), .enable("false")) multiplexer_4 (
    .in0(r_shift8), .in1({{9{r_shift8[15]}}, r_shift8[14:8]}));  // open: out, sel

  // Other names for the same wires on the sheet: r_shift1[15:0] = data_in;
  //   r_shifted1[15:0] = {{2{data_in[15]}}, data_in[14:1]}; r_shifted2[15:0] = {{3{r_shift2[15]}}, r_shift2[14:2]};
  //   r_shifted4[15:0] = {{5{r_shift4[15]}}, r_shift4[14:4]}; r_shifted8[15:0] = {{9{r_shift8[15]}}, r_shift8[14:8]}
endmodule

module L_Shifter (
  input  [15:0] data_in,
  input  [2:0] bitstoShift,
  output [15:0] shifted_data
);

  wire [15:0] Lshift2, Lshift4, Lshift8;

  Multiplexer #(.width(16), .enable("false")) multiplexer_1 (
    .in0(data_in), .in1({data_in[14:0], 1'b0}), .out(Lshift2), .sel(bitstoShift[0]));
  Multiplexer #(.width(16), .enable("false")) multiplexer_2 (
    .in0(Lshift2), .in1({Lshift2[13:0], 2'b00}), .out(Lshift4), .sel(bitstoShift[1]));
  Multiplexer #(.width(16), .enable("false")) multiplexer_3 (
    .in0(Lshift4), .in1({Lshift4[11:0], 4'b0000}), .out(shifted_data), .sel(bitstoShift[2]));
  Multiplexer #(.width(16), .enable("false")) multiplexer_4 (
    .in0(Lshift8), .in1({Lshift8[7:0], {8{1'b0}}}));  // open: out, sel

  // Other names for the same wires on the sheet: Lshift1[15:0] = data_in; Lshifted1[15:1] = data_in[14:0];
  //   Lshifted2[15:2] = Lshift2[13:0]; Lshifted4[15:4] = Lshift4[11:0]; Lshifted8[15:8] = Lshift8[7:0]
endmodule

module memoryLatch (
  input  [15:0] adress,
  input  WE,
  input  clk,
  input  [15:0] dataIn,
  output [15:0] address_latched,
  output WE_latched,
  output OE_latched,
  output [15:0] data_in_latched
);

  wire d_ff_1_q;
  wire [15:0] register_1_q;

  Register #(.width(16), .trigger("falling")) register_1 (
    .D(adress), .en(WE), .clk(clk), .Q(register_1_q));  // open: clr
  D_Flip_Flop #(.trigger("falling")) d_ff_1 (.D(WE), .clk(clk), .Q(d_ff_1_q));  // open: Qn, preset, reset
  Register #(.width(16), .trigger("falling")) register_2 (
    .D(dataIn), .en(WE), .clk(clk), .Q(data_in_latched));  // open: clr
  Multiplexer #(.width(16), .enable("false")) multiplexer_1 (
    .in0(adress), .in1(register_1_q), .out(address_latched), .sel(d_ff_1_q));
  and and_1 (WE_latched, clk, d_ff_1_q);
  not not_1 (OE_latched, WE_latched);
endmodule

module signX (
  input  [5:0] Imm,
  output [15:0] signX
);


  assign signX = {{11{Imm[5]}}, Imm[4:0]};
endmodule

module contrl (
  input  [15:0] Input,
  input  WE,
  output RegWE,
  output [2:0] opType,
  output [2:0] sft,
  output [2:0] Rs,
  output [2:0] Rt,
  output [5:0] Imm,
  output [11:0] addr,
  output [2:0] rd,
  output lw_enb,
  output beq_enb,
  output bgt_enb,
  output mem_WE,
  output TTY_enb,
  output KB_enb,
  output I_enb,
  output J_enb,
  output jr_enb,
  output jal_enb
);

  wire o6, o7, o8, o9, o10, o11, o12, o13, or_2_out, or_4_out, or_5_out;

  Decoder #(.select(4)) decoder_1 (
    .out0(TTY_enb), .out1(KB_enb), .out2(lw_enb), .out3(mem_WE), .out4(beq_enb), .out5(bgt_enb), .out6(o6),
    .out7(o7), .out8(o8), .out9(o9), .out10(o10), .out11(o11), .out12(o12), .out13(o13), .out14(jal_enb),
    .out15(jr_enb), .sel(Input[15:12]), .en(WE));
  or or_1 (J_enb, o13, jal_enb);
  or or_2 (or_2_out, o10, bgt_enb, beq_enb);
  assign opType = o11 ? 3'b010 : 3'bz;  // Controlled_Buffer shiftRight
  assign opType = o12 ? 3'b011 : 3'bz;  // Controlled_Buffer shiftLeft
  assign opType = o6 ? 3'b100 : 3'bz;  // Controlled_Buffer or_3
  assign opType = o7 ? 3'b101 : 3'bz;  // Controlled_Buffer and
  assign opType = or_4_out ? 3'b110 : 3'bz;  // Controlled_Buffer and_2
  or or_4 (or_4_out, jr_enb, jal_enb, o13, KB_enb, TTY_enb);
  assign opType = or_5_out ? 3'b000 : 3'bz;  // Controlled_Buffer add
  or or_5 (or_5_out, mem_WE, lw_enb, o9, o8);
  assign opType = or_2_out ? 3'b001 : 3'bz;  // Controlled_Buffer sub
  or or_6 (I_enb, lw_enb, mem_WE, o8);
  or or_7 (RegWE, KB_enb, lw_enb, o6, o7, o8, o9, o10, o11, o12, jal_enb);

  assign addr = Input[11:0];
  assign Imm = Input[5:0];
  assign rd = Input[5:3];
  assign Rs = Input[11:9];
  assign Rt = Input[8:6];
  assign sft = Input[2:0];

  // Other names for the same wires on the sheet: J = J_enb; o0 = TTY_enb; o1 = KB_enb; o2 = lw_enb; o3 = mem_WE;
  //   o4 = beq_enb; o5 = bgt_enb; o14 = jal_enb; o15 = jr_enb; opC[3:0] = Input[15:12]; r0 = Input[0];
  //   restC[11:0] = Input[11:0]; Shmt[2:0] = Input[2:0]; r1 = Input[1]; r2 = Input[2]; r3 = Input[3]; r4 = Input[4];
  //   r5 = Input[5]; r6 = Input[6]; r7 = Input[7]; r8 = Input[8]; r9 = Input[9]; r10 = Input[10]; r11 = Input[11]
endmodule
